# Fritzing sketch Pavlov1 (saved by Fritzing 1.0.2b)
circuit board: 8.46667cm x 5.64444cm
breadboards: 1

parts:
  J1 = Power Jack [package=power_jack_smd]
  IC1 = L293D [package=THT]
  Stepper = 28BYJ-48 Stepper Motor [part_number=28BYJ-48]
  LCD2004-I2C1 = LCD2004-I2C
  U1 = LuaNode32 / ESP32 [part_number=ESP32S-PIN30]
  Gate_Servo = Basic Servo
  S1 = Toggle Switch [package=THT]
  LCD = Header 4 [package=screwterminal-3.5mm-4_lock]
  Serial = Header 4 [package=screwterminal-3.5mm-4_lock]

nets (from the breadboard view):
  N1: J1.PWR, S1.L1
  GND: J1.GND, IC1.0V, LCD2004-I2C1.GND, U1.D13, U1.GND, Gate_Servo.gnd, LCD.1, Serial.2
  VCC: IC1.Enable_1, IC1.+Vmotor, IC1.Enable_2, IC1.+V, LCD2004-I2C1.VCC, U1.Vin, S1.COM, LCD.2
  N2: IC1.In_1, U1.D15
  N3: IC1.Out_1_(_Controlled_by_Enable_1_), Stepper.orange-pin
  N4: IC1.Out_2_(_Controlled_by_Enable_1_), Stepper.pink-pin
  N5: IC1.In_2, U1.D14, U1.D12
  N6: IC1.In_3, U1.D26, U1.D27
  N7: IC1.Out_3_(_Controlled_by_Enable_2_), Stepper.yellow-pin
  N8: IC1.Out_4_(_Controlled_by_Enable_2_), Stepper.blue-pin
  N9: IC1.In_4, U1.D4, U1.RX2
  N10: LCD2004-I2C1.SDA, U1.D21, LCD.3
  N11: LCD2004-I2C1.SCL, U1.D22, U1.D23, LCD.4
  N12: U1.3V3, Serial.1
  N13: U1.D2, Gate_Servo.pulse
  N14: U1.RX0, Serial.3
  N15: U1.TX0, Serial.4

custom parts:
  28BYJ-48 Stepper Motor: Unipolar Stepper Motor 28BYJ-48 Top coil - pink & orange Bottom coil - blue & yellow Common rail - red Connector pins: blue - pink - yellow - orange - red
  LCD2004-I2C: A standard character display with 4x20 characters. Comes in many colors with LCM2004 IIC attached.
  LuaNode32 / ESP32: New Image for LuaNode32 DOIT ESP32 DEVKIT V1. Base parts from LuaNode32 / ESP32 ESP32 based LuaNode32 by G.Noorlander DOIT Esp32 DevKit v1 (30 pins long, 11 pins width) by Werner Rothschopf (modified by vanepp Dec 2018)
